# Fritzing sketch 10-MQ5 (saved by Fritzing 0.9.4)
breadboards: 1

parts:
  Mod1 = MQ-7 breakout
  Part1 = Arduino Uno (Rev3)

nets:
  VCC: Mod1.VCC, Part1.5V
  GND: Mod1.GND, Part1.GND
  N1: Mod1.DO, Part1.D8
  N2: Mod1.AO, Part1.A0

custom parts:
  MQ-7 breakout: MQ-5 gas sensor
